# Fritzing sketch Sketch (saved by Fritzing 0.9.4)

parts:
  WeMos_D1_Mini1 = WeMos D1 Mini
  R1 = Temperature Sensor (Thermistor) [thermistor_type=NTC package=THT]
  Mod1 = OLED Mono 0.56 inch blue or white
  YF-B4_Flow_Meter = YF-S201 Water Flow Meter
  R2 = Resistor [tolerance=±5% resistance=47k package=THT]

nets:
  N1: WeMos_D1_Mini1.3V3, R1.pin_0
  VCC: WeMos_D1_Mini1.5V, Mod1.VCC, YF-B4_Flow_Meter.VCC
  N2: WeMos_D1_Mini1.A0, R1.pin_1, R2.Pin_0
  N3: WeMos_D1_Mini1.D1, Mod1.SCL
  N4: WeMos_D1_Mini1.D2, Mod1.SDA
  N5: WeMos_D1_Mini1.D5, YF-B4_Flow_Meter.SIG
  GND: WeMos_D1_Mini1.G, Mod1.GND, YF-B4_Flow_Meter.GND, R2.Pin_1

custom parts:
  OLED Mono 0.56 inch blue or white: OLED, I2C 3.3V - 5V Blue and White text versions
  YF-S201 Water Flow Meter: The YF-S201 Flow Meter. The input voltage is 5V to 24V (DC).
